// Logisim project 3 bit encoder.circ as structural Verilog: 1 circuit, main circuit main
module main (
  input  in_1,
  input  in_2,
  input  in_3,
  output _0,
  output _1,
  output _2,
  output _3,
  output _4,
  output _5,
  output _6,
  output _7
);

  wire not_1_out, not_2_out, not_3_out;

  not not_1 (not_1_out, in_1);
  not not_2 (not_2_out, in_2);
  not not_3 (not_3_out, in_3);
  and and_1 (_0, not_1_out, not_2_out, not_3_out);
  and and_2 (_1, in_1, not_2_out, not_3_out);
  and and_3 (_2, in_2, not_1_out, not_3_out);
  and and_4 (_3, not_3_out, in_1, in_2);
  and and_5 (_4, not_1_out, in_3, not_2_out);
  and and_6 (_5, in_1, in_3, not_2_out);
  and and_7 (_6, not_1_out, not_1_out, in_2);
  and and_8 (_7, in_1, in_2, in_3);

  // Notes on the sheet:
  //   3 bit decoder
endmodule
