// Logisim project adders.circ as structural Verilog: 1 circuit, main circuit main
module main (
  input  A,
  input  B,
  input  A_2,
  input  B_2,
  input  Cary,
  output C,
  output Cary_2,
  output out_8,
  output out_9
);

  wire and_2_out, and_3_out, xor_2_out;

  xor xor_1 (C, A, B);
  and and_1 (Cary_2, A, B);
  xor xor_2 (xor_2_out, A_2, B_2);
  and and_2 (and_2_out, A_2, B_2);
  and and_3 (and_3_out, xor_2_out, Cary);
  xor xor_3 (out_8, xor_2_out, Cary);
  or or_1 (out_9, and_3_out, and_2_out);

  // Notes on the sheet:
  //   Half Adder
  //   Full Adder
endmodule
